# Fritzing sketch Fire And Gas Alarm System (saved by Fritzing 0.9.5d)
breadboards: 2

parts:
  Mod1 = KY-026 Flame Sensor Module [package="Breakout board"]
  Display1 = LCD screen 16x2 HD44780
  Part1 = MQ-3 breakout
  LED1 = smd LED [color="Red (633nm)" package="0805 [SMD]"]
  LED2 = smd LED [color="Green (560nm)" package="0805 [SMD]"]
  U2 = Voltage Regulator - 5V [package="DPak [SMD]"]
  VCC1 = Battery
  µC1 = ATmega32 [package=dip]
  U3 = POT [package=alps_pot]
  Y1 = CRYSTAL [package=crystal-smd-5x3]
  C1 = Capacitor Polarized [package=cpol-radial-100uf-25v]
  C2 = Capacitor Polarized [package=cpol-radial-100uf-25v]

nets:
  N1: Mod1.A0, µC1.PA0
  N2: Mod1.G, Part1.GND, U2.output_voltage
  N3: Display1.VSS, Display1.R_W, Display1.DB0, Display1.DB1, Display1.DB2, Display1.DB3, Display1.K, U3.A
  N4: Display1.VDD, Display1.A, U3.E
  N5: Display1.VO, U3.S
  N6: Display1.RS, µC1.PB1
  N7: Display1.E, µC1.PB0
  N8: Display1.DB4, µC1.PB4
  N9: Display1.DB5, µC1.PB5
  N10: Display1.DB6, µC1.PB6
  N11: Display1.DB7, µC1.PB7
  N12: LED1.cathode, LED2.cathode, U2.GND, VCC1.-, C1.+, C2.-
  N13: LED1.anode, µC1.PC0
  N14: LED2.anode, µC1.PC1
  N15: U2.input_voltage, VCC1.+
  GND1: µC1.GND1, µC1.GND2
  N16: µC1.XTAL2, Y1.1, C2.+
  N17: µC1.XTAL1, Y1.2, C1.-

custom parts:
  KY-026 Flame Sensor Module: KY-026 Flame Sensor Module reacts in the presence of fire.
  LCD screen 16x2 HD44780: LCD screen with HD44780 controller enables showing text, symbols, value or anything else that comes from Croduino/Arduino. It is capable of showing 16 symbols in two lines and therefore can be used in many projects that need to send clearly visible and legible output information.. • Color of symbols: White • Backlight: Blue • Dimensions: 80 x 36 x 12 mm • Screen dimensions: 64.5 x 16 mm •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
  MQ-3 breakout: Alcohol sensor is capable of detecting alcohol (ethanol) particles on itself and gives the information in digital form back to us to manipulate with it. SKU:101251 • Voltage: 5V DC • Power: max 750mW • Measurement range: 0.04-4mg/L
  ATmega32: AVR 8-bit microcontroller.
